// Digital circuit Lab01.dig as structural Verilog
module Lab01 (
  input  B,
  input  C,
  input  A,
  input  D,
  output Fg,
  output Ff,
  output Fe,
  output Fd,
  output Fc,
  output Fb,
  output Fa
);

  wire and_1_out, and_2_out, and_3_out, and_4_out, and_5_out, and_6_out, and_7_out, and_8_out, and_9_out,
       and_10_out, and_11_out, and_12_out, and_13_out, and_14_out, and_15_out, and_16_out, and_17_out,
       and_18_out, and_19_out, and_20_out, and_21_out, and_22_out, and_23_out, and_24_out, and_25_out,
       and_26_out, and_27_out, and_28_out, and_29_out, and_30_out, and_31_out, and_32_out, not_1_out,
       not_2_out, not_3_out, not_4_out, not_5_out, not_6_out, not_7_out, not_8_out, not_9_out, not_10_out,
       not_11_out, not_12_out, not_13_out, not_14_out, not_15_out, not_16_out, not_17_out, not_18_out,
       not_19_out, not_20_out, not_21_out, not_22_out, not_23_out, not_24_out, not_25_out, not_26_out,
       not_27_out, not_28_out, not_29_out, not_30_out, not_31_out, not_32_out, not_33_out, not_34_out,
       not_35_out, not_36_out, not_37_out, not_38_out, not_39_out, not_40_out, not_41_out, not_42_out,
       not_43_out;

  not not_1 (not_1_out, B);
  not not_2 (not_2_out, C);
  not not_3 (not_3_out, A);
  not not_4 (not_4_out, A);
  not not_5 (not_5_out, B);
  not not_6 (not_6_out, D);
  not not_7 (not_7_out, A);
  not not_8 (not_8_out, B);
  not not_9 (not_9_out, A);
  not not_10 (not_10_out, C);
  not not_11 (not_11_out, D);
  not not_12 (not_12_out, A);
  not not_13 (not_13_out, B);
  not not_14 (not_14_out, D);
  not not_15 (not_15_out, C);
  not not_16 (not_16_out, A);
  not not_17 (not_17_out, C);
  not not_18 (not_18_out, C);
  not not_19 (not_19_out, B);
  not not_20 (not_20_out, A);
  not not_21 (not_21_out, A);
  not not_22 (not_22_out, A);
  not not_23 (not_23_out, B);
  not not_24 (not_24_out, D);
  not not_25 (not_25_out, C);
  not not_26 (not_26_out, C);
  not not_27 (not_27_out, B);
  not not_28 (not_28_out, D);
  not not_29 (not_29_out, D);
  not not_30 (not_30_out, B);
  not not_31 (not_31_out, C);
  not not_32 (not_32_out, D);
  not not_33 (not_33_out, A);
  not not_34 (not_34_out, C);
  not not_35 (not_35_out, D);
  not not_36 (not_36_out, A);
  not not_37 (not_37_out, C);
  not not_38 (not_38_out, A);
  not not_39 (not_39_out, D);
  not not_40 (not_40_out, B);
  not not_41 (not_41_out, B);
  not not_42 (not_42_out, C);
  not not_43 (not_43_out, D);
  and and_1 (and_1_out, A, not_1_out, not_2_out);
  and and_2 (and_2_out, not_3_out, B, D);
  and and_3 (and_3_out, B, C);
  and and_4 (and_4_out, not_4_out, C);
  and and_5 (and_5_out, not_5_out, not_6_out);
  and and_6 (and_6_out, not_7_out, not_8_out);
  and and_7 (and_7_out, not_9_out, not_10_out, not_11_out);
  and and_8 (and_8_out, not_12_out, C, D);
  and and_9 (and_9_out, A, not_13_out, not_14_out);
  and and_10 (and_10_out, A, not_15_out, D);
  and and_11 (and_11_out, not_16_out, not_17_out);
  and and_12 (and_12_out, not_18_out, D);
  and and_13 (and_13_out, A, not_19_out);
  and and_14 (and_14_out, not_20_out, D);
  and and_15 (and_15_out, not_21_out, B);
  and and_16 (and_16_out, not_22_out, not_23_out, not_24_out);
  and and_17 (and_17_out, A, not_25_out);
  and and_18 (and_18_out, B, not_26_out, D);
  and and_19 (and_19_out, not_27_out, C, D);
  and and_20 (and_20_out, B, C, not_28_out);
  and and_21 (and_21_out, A, B);
  and and_22 (and_22_out, C, not_29_out);
  and and_23 (and_23_out, not_30_out, not_32_out);
  and and_24 (and_24_out, A, C);
  and and_25 (and_25_out, not_33_out, not_34_out, not_35_out);
  and and_26 (and_26_out, not_36_out, B, not_37_out);
  and and_27 (and_27_out, not_38_out, B, not_39_out);
  and and_28 (and_28_out, A, not_40_out);
  and and_29 (and_29_out, A, C);
  and and_30 (and_30_out, not_41_out, C);
  and and_31 (and_31_out, B, not_42_out);
  and and_32 (and_32_out, C, not_43_out);
  or or_1 (Fa, and_1_out, and_2_out, and_3_out, and_4_out, and_5_out);
  or or_2 (Fb, and_6_out, and_7_out, and_8_out, and_9_out, and_10_out);
  or or_3 (Fc, and_11_out, and_12_out, and_13_out, and_14_out, and_15_out);
  or or_4 (Fd, and_16_out, and_17_out, and_18_out, and_19_out, and_20_out);
  or or_5 (Fe, and_21_out, and_22_out, and_23_out, and_24_out);
  or or_6 (Ff, and_25_out, and_26_out, and_27_out, and_28_out, and_29_out);
  or or_7 (Fg, A, and_30_out, and_31_out, and_32_out);
  Seven_Seg seven_seg_1 (.a(Fa), .b(Fb), .c(Fc), .d(Fd), .e(Fe), .f(Ff), .g(Fg), .dp(1'b0));
endmodule
