// Digital circuit Lab02.dig as structural Verilog
module Lab02 (
  input  CLK,
  input  Y,
  output QC,
  output QB,
  output QA
);

  wire and_1_out, and_2_out;

  and and_1 (and_1_out, Y, QB, QA);
  T_FF TC (.T(and_1_out), .C(CLK), .Q(QC));  // open: nQ
  T_FF TB (.T(and_2_out), .C(CLK), .Q(QB));  // open: nQ
  and and_2 (and_2_out, Y, QA);
  T_FF TA (.T(Y), .C(CLK), .Q(QA));  // open: nQ
endmodule
