// Digital circuit Lab03_ALU_Efficient.dig as structural Verilog
module Lab03_ALU_Efficient (
  input  A1,
  input  A2,
  input  A3,
  input  A0,
  input  B0,
  input  B1,
  input  B2,
  input  B3,
  input  Math,
  input  Sub,
  input  CLK,
  input  Enable,
  output C0,
  output C1,
  output C2,
  output C3
);

  wire add_1_c_o, add_1_s, add_2_c_o, add_2_s, add_3_c_o, add_3_s, add_4_s, and_1_out, and_2_out, and_3_out,
       and_4_out, multiplexer_1_out, multiplexer_2_out, multiplexer_3_out, multiplexer_4_out,
       multiplexer_5_out, multiplexer_6_out, multiplexer_7_out, multiplexer_8_out, not_1_out, or_1_out,
       or_2_out, or_3_out, or_4_out, register_1_q, register_2_q, register_3_q, register_4_q, register_9_q,
       register_10_q, register_11_q, register_12_q, xor_1_out, xor_2_out, xor_3_out, xor_4_out;

  not not_1 (not_1_out, CLK);
  Add add_1 (.a(register_4_q), .b(xor_1_out), .c_i(Sub), .s(add_1_s), .c_o(add_1_c_o));
  xor xor_1 (xor_1_out, Sub, register_12_q);
  Add add_2 (.a(register_3_q), .b(xor_2_out), .c_i(add_1_c_o), .s(add_2_s), .c_o(add_2_c_o));
  xor xor_2 (xor_2_out, Sub, register_11_q);
  xor xor_3 (xor_3_out, Sub, register_10_q);
  Add add_3 (.a(register_2_q), .b(xor_3_out), .c_i(add_2_c_o), .s(add_3_s), .c_o(add_3_c_o));
  Register register_1 (.D(A3), .C(CLK), .en(Enable), .Q(register_1_q));
  Add add_4 (.a(register_1_q), .b(xor_4_out), .c_i(add_3_c_o), .s(add_4_s));  // open: c_o
  Register register_2 (.D(A2), .C(CLK), .en(Enable), .Q(register_2_q));
  xor xor_4 (xor_4_out, Sub, register_9_q);
  Register register_3 (.D(A1), .C(CLK), .en(Enable), .Q(register_3_q));
  Register register_4 (.D(A0), .C(CLK), .en(Enable), .Q(register_4_q));
  Multiplexer multiplexer_1 (.sel(Math), .in_0(multiplexer_5_out), .in_1(add_4_s), .out(multiplexer_1_out));
  Register register_5 (.D(multiplexer_1_out), .C(not_1_out), .en(Enable), .Q(C3));
  Multiplexer multiplexer_2 (.sel(Math), .in_0(multiplexer_6_out), .in_1(add_3_s), .out(multiplexer_2_out));
  Register register_6 (.D(multiplexer_2_out), .C(not_1_out), .en(Enable), .Q(C2));
  Multiplexer multiplexer_3 (.sel(Math), .in_0(multiplexer_7_out), .in_1(add_2_s), .out(multiplexer_3_out));
  Register register_7 (.D(multiplexer_3_out), .C(not_1_out), .en(Enable), .Q(C1));
  Multiplexer multiplexer_4 (.sel(Math), .in_0(multiplexer_8_out), .in_1(add_1_s), .out(multiplexer_4_out));
  Register register_8 (.D(multiplexer_4_out), .C(not_1_out), .en(Enable), .Q(C0));
  or or_1 (or_1_out, register_9_q, register_1_q);
  or or_2 (or_2_out, register_10_q, register_2_q);
  Multiplexer multiplexer_5 (.sel(Sub), .in_0(and_1_out), .in_1(or_1_out), .out(multiplexer_5_out));
  or or_3 (or_3_out, register_11_q, register_3_q);
  or or_4 (or_4_out, register_12_q, register_4_q);
  Multiplexer multiplexer_6 (.sel(Sub), .in_0(and_2_out), .in_1(or_2_out), .out(multiplexer_6_out));
  and and_1 (and_1_out, register_9_q, register_1_q);
  Multiplexer multiplexer_7 (.sel(Sub), .in_0(and_3_out), .in_1(or_3_out), .out(multiplexer_7_out));
  and and_2 (and_2_out, register_10_q, register_2_q);
  Multiplexer multiplexer_8 (.sel(Sub), .in_0(and_4_out), .in_1(or_4_out), .out(multiplexer_8_out));
  and and_3 (and_3_out, register_11_q, register_3_q);
  and and_4 (and_4_out, register_12_q, register_4_q);
  Register register_9 (.D(B3), .C(CLK), .en(Enable), .Q(register_9_q));
  Register register_10 (.D(B2), .C(CLK), .en(Enable), .Q(register_10_q));
  Register register_11 (.D(B1), .C(CLK), .en(Enable), .Q(register_11_q));
  Register register_12 (.D(B0), .C(CLK), .en(Enable), .Q(register_12_q));
endmodule
