// Digital circuit Lab03_RAM.dig as structural Verilog
module Lab03_RAM (
  input  [3:0] Data,
  input  CLK,
  input  [3:0] ADR,
  input  ADRRegEnable,
  input  Write,
  input  Lookup,
  input  DataRegEnable,
  output [3:0] Output
);

  wire [3:0] ramdualport_1_d, register_1_q;

  Register #(.Bits(4)) register_1 (.D(ADR), .C(CLK), .en(ADRRegEnable), .Q(register_1_q));
  RAMDualPort #(.AddrBits(4), .Bits(4)) ramdualport_1 (
    .A(register_1_q), .Din(Data), .str(Write), .C(CLK), .ld(Lookup), .D(ramdualport_1_d));
  Register #(.Bits(4)) register_2 (.D(ramdualport_1_d), .C(CLK), .en(DataRegEnable), .Q(Output));
endmodule
