// Digital circuit Lab03b.dig as structural Verilog
module Lab03b (
  input  Math,
  input  Sub,
  input  CLK,
  input  [3:0] ADR,
  input  ADRRegEnable,
  input  Write,
  input  Lookup,
  input  [10:0] Data,
  input  RegEnable,
  input  Prog,
  input  CounterEnable,
  output C0,
  output C1,
  output C2,
  output C3
);

  wire add_1_c_o, add_1_s, add_2_c_o, add_2_s, add_3_c_o, add_3_s, add_4_s, and_1_out, and_2_out, and_3_out,
       and_4_out, and_5_out, and_6_out, and_7_out, multiplexer_1_out, multiplexer_2_out, multiplexer_3_out,
       multiplexer_4_out, multiplexer_5_out, multiplexer_7_out, multiplexer_8_out, multiplexer_12_out,
       multiplexer_14_out, multiplexer_15_out, multiplexer_16_out, not_1_out, or_1_out, or_2_out, or_3_out,
       or_4_out, register_2_q, register_3_q, register_4_q, register_5_q, xor_1_out, xor_2_out, xor_3_out,
       xor_4_out;
  wire [3:0] multiplexer_6_out, register_1_q, TC_2_q;
  wire [10:0] ramdualport_1_d;

  T_FF TA (.T(multiplexer_1_out), .C(CLK), .Q(TC_2_q[0]));  // open: nQ
  and and_1 (and_1_out, multiplexer_1_out, TC_2_q[0]);
  T_FF TB (.T(and_1_out), .C(CLK), .Q(TC_2_q[1]));  // open: nQ
  and and_2 (and_2_out, multiplexer_1_out, TC_2_q[1], TC_2_q[0]);
  T_FF TC (.T(and_2_out), .C(CLK), .Q(TC_2_q[2]));  // open: nQ
  and and_3 (and_3_out, multiplexer_1_out, TC_2_q[2], TC_2_q[1], TC_2_q[0]);
  T_FF TC_2 (.T(and_3_out), .C(CLK), .Q(TC_2_q[3]));  // open: nQ
  Multiplexer multiplexer_1 (.sel(Prog), .in_0(ramdualport_1_d[10]), .in_1(CounterEnable), .out(multiplexer_1_out));
  Multiplexer multiplexer_2 (.sel(Prog), .in_0(ramdualport_1_d[9]), .in_1(RegEnable), .out(multiplexer_2_out));
  Multiplexer multiplexer_3 (.sel(Prog), .in_0(ramdualport_1_d[8]), .in_1(ADRRegEnable), .out(multiplexer_3_out));
  Multiplexer multiplexer_4 (.sel(Prog), .in_0(ramdualport_1_d[7]), .in_1(Write), .out(multiplexer_4_out));
  Multiplexer multiplexer_5 (.sel(Prog), .in_0(ramdualport_1_d[6]), .in_1(Lookup), .out(multiplexer_5_out));
  Multiplexer #(.Bits(4)) multiplexer_6 (.sel(Prog), .in_0(TC_2_q), .in_1(ADR), .out(multiplexer_6_out));
  Multiplexer multiplexer_7 (.sel(Prog), .in_0(ramdualport_1_d[5]), .in_1(Sub), .out(multiplexer_7_out));
  Multiplexer multiplexer_8 (.sel(Prog), .in_0(ramdualport_1_d[4]), .in_1(Math), .out(multiplexer_8_out));
  Register #(.Bits(4)) register_1 (.D(multiplexer_6_out), .C(CLK), .en(multiplexer_3_out), .Q(register_1_q));
  RAMDualPort #(.AddrBits(4), .Bits(11)) ramdualport_1 (
    .A(register_1_q), .Din(Data), .str(multiplexer_4_out), .C(CLK), .ld(multiplexer_5_out),
    .D(ramdualport_1_d));
  not not_1 (not_1_out, CLK);
  Add add_1 (.a(register_5_q), .b(xor_1_out), .c_i(multiplexer_7_out), .s(add_1_s), .c_o(add_1_c_o));
  xor xor_1 (xor_1_out, multiplexer_7_out, ramdualport_1_d[0]);
  xor xor_2 (xor_2_out, multiplexer_7_out, ramdualport_1_d[1]);
  Add add_2 (.a(register_4_q), .b(xor_2_out), .c_i(add_1_c_o), .s(add_2_s), .c_o(add_2_c_o));
  Add add_3 (.a(register_3_q), .b(xor_3_out), .c_i(add_2_c_o), .s(add_3_s), .c_o(add_3_c_o));
  xor xor_3 (xor_3_out, multiplexer_7_out, ramdualport_1_d[2]);
  Register register_2 (.D(C3), .C(not_1_out), .en(multiplexer_2_out), .Q(register_2_q));
  xor xor_4 (xor_4_out, multiplexer_7_out, ramdualport_1_d[3]);
  Add add_4 (.a(register_2_q), .b(xor_4_out), .c_i(add_3_c_o), .s(add_4_s));  // open: c_o
  Register register_3 (.D(C2), .C(not_1_out), .en(multiplexer_2_out), .Q(register_3_q));
  Register register_4 (.D(C1), .C(not_1_out), .en(multiplexer_2_out), .Q(register_4_q));
  Register register_5 (.D(C0), .C(not_1_out), .en(multiplexer_2_out), .Q(register_5_q));
  Multiplexer multiplexer_9 (.sel(multiplexer_8_out), .in_0(multiplexer_12_out), .in_1(add_4_s), .out(C3));
  Multiplexer multiplexer_10 (.sel(multiplexer_8_out), .in_0(multiplexer_14_out), .in_1(add_3_s), .out(C2));
  or or_1 (or_1_out, ramdualport_1_d[3], register_2_q);
  Multiplexer multiplexer_11 (.sel(multiplexer_8_out), .in_0(multiplexer_15_out), .in_1(add_2_s), .out(C1));
  or or_2 (or_2_out, ramdualport_1_d[2], register_3_q);
  Multiplexer multiplexer_12 (.sel(multiplexer_7_out), .in_0(and_4_out), .in_1(or_1_out), .out(multiplexer_12_out));
  Multiplexer multiplexer_13 (.sel(multiplexer_8_out), .in_0(multiplexer_16_out), .in_1(add_1_s), .out(C0));
  or or_3 (or_3_out, ramdualport_1_d[1], register_4_q);
  or or_4 (or_4_out, ramdualport_1_d[0], register_5_q);
  Multiplexer multiplexer_14 (.sel(multiplexer_7_out), .in_0(and_5_out), .in_1(or_2_out), .out(multiplexer_14_out));
  and and_4 (and_4_out, ramdualport_1_d[3], register_2_q);
  Multiplexer multiplexer_15 (.sel(multiplexer_7_out), .in_0(and_6_out), .in_1(or_3_out), .out(multiplexer_15_out));
  and and_5 (and_5_out, ramdualport_1_d[2], register_3_q);
  and and_6 (and_6_out, ramdualport_1_d[1], register_4_q);
  Multiplexer multiplexer_16 (.sel(multiplexer_7_out), .in_0(and_7_out), .in_1(or_4_out), .out(multiplexer_16_out));
  and and_7 (and_7_out, ramdualport_1_d[0], register_5_q);

  // Notes on the sheet:
  //   Program Counter
  //   Control
  //   MAR and RAM
  //   ALU
endmodule
